// Logisim project H1.circ as structural Verilog: 10 circuits, main circuit P1
module P1 (
  input  I3,
  input  I2,
  input  I1,
  input  I0,
  output A,
  output B,
  output C,
  output D,
  output E,
  output F,
  output G,
  output H,
  output I,
  output J,
  output K,
  output L,
  output M,
  output N,
  output O,
  output P
);

  wire not_1_out, not_2_out, not_3_out, not_4_out;

  not not_1 (not_1_out, I2);
  not not_2 (not_2_out, I3);
  not not_3 (not_3_out, I1);
  not not_4 (not_4_out, I0);
  and and_1 (A, not_4_out, not_3_out, not_1_out, not_2_out);
  and and_2 (B, I0, not_3_out, not_1_out, not_2_out);
  and and_3 (C, I1, not_4_out, not_1_out, not_2_out);
  and and_4 (D, I0, not_4_out, not_1_out, not_2_out);
  and and_5 (E, I2, not_4_out, not_3_out, not_2_out);
  and and_6 (F, I0, I2, not_3_out, not_2_out);
  and and_7 (G, I1, I2, not_4_out, not_2_out);
  and and_8 (H, I0, I1, I2, not_2_out);
  and and_9 (I, I3, not_4_out, not_3_out, not_1_out);
  and and_10 (J, I0, I3, not_3_out, not_1_out);
  and and_11 (K, I1, I3, not_4_out, not_1_out);
  and and_12 (L, I0, I1, I3, not_1_out);
  and and_13 (M, I2, I3, not_4_out, not_3_out);
  and and_14 (N, I0, I2, I3, not_3_out);
  and and_15 (O, I1, I2, I3, not_4_out);
  and and_16 (P, I0, I1, I2, I3);

  // Notes on the sheet:
  //   PROBLEM 1: DECODER
  //   INPUT SECTION: Do not change anything here!
  //   You may only change the values of the inputs for testing using the hand tool.
  //   Do not introduce any other input or output pins.
  //   To your logic
  //   OUTPUT SECTION: Do not change anything here!
  //   Do not introduce any other input or output pins.
  //   From your logic
endmodule

module P2 (
  input  A,
  input  B,
  input  C,
  output X,
  output Y
);

  wire and_2_out, and_3_out, and_4_out, and_5_out, and_6_out, and_7_out, not_1_out, not_2_out, not_3_out,
       not_4_out, not_5_out, not_6_out, not_7_out, not_8_out, not_9_out;

  not not_1 (not_1_out, A);
  not not_2 (not_2_out, B);
  // AND_Gate and_1 has open pins: in0=C, in1=B, in2=A, out=open
  and and_2 (and_2_out, not_1_out, not_2_out, C);
  not not_3 (not_3_out, A);
  and and_3 (and_3_out, not_3_out, B, not_4_out);
  not not_4 (not_4_out, C);
  not not_5 (not_5_out, A);
  and and_4 (and_4_out, not_5_out, B, C);
  and and_5 (and_5_out, A, not_6_out, not_7_out);
  not not_6 (not_6_out, B);
  not not_7 (not_7_out, C);
  and and_6 (and_6_out, A, not_8_out, C);
  not not_8 (not_8_out, B);
  and and_7 (and_7_out, A, B, not_9_out);
  not not_9 (not_9_out, C);
  // AND_Gate and_8 has open pins: in0=A, in1=B, in2=C, out=open
  or or_1 (X, and_3_out, and_4_out, and_7_out);
  or or_2 (Y, and_2_out, and_5_out, and_6_out);

  // Notes on the sheet:
  //   PROBLEM 2: PROGRAMMABLE LOGIC ARRAY
  //   INPUT SECTION: Do not change anything here!
  //   You may only change the values of the inputs for testing using the hand tool.
  //   Do not introduce any other input or output pins.
  //   To your logic
  //   OUTPUT SECTION: Do not change anything here!
  //   Do not introduce any other input or output pins.
  //   From your logic
endmodule

module P3 (
  input  A,
  input  B,
  input  C,
  output X
);

  wire transistor_1_out, transistor_2_out, transistor_7_out, transistor_8_out;

  Transistor transistor_1 (.in(transistor_2_out), .out(transistor_1_out), .gate(A));
  Transistor transistor_2 (.in(1'b1), .out(transistor_2_out), .gate(C));
  Transistor transistor_3 (.in(1'b1), .out(transistor_2_out), .gate(A));
  Transistor transistor_4 (.in(transistor_2_out), .out(transistor_1_out), .gate(B));
  Transistor transistor_5 (.in(transistor_1_out), .out(X), .gate(C));
  Transistor transistor_6 (.in(transistor_2_out), .out(transistor_1_out), .gate(C));
  Transistor transistor_7 (.in(1'b1), .out(transistor_7_out), .gate(A));
  Transistor transistor_8 (.in(transistor_7_out), .out(transistor_8_out), .gate(C));
  Transistor transistor_9 (.in(transistor_7_out), .out(X), .gate(B));
  Transistor transistor_10 (.in(transistor_8_out), .out(X), .gate(A));

  // Other names for the same wires on the sheet: tA = A; tB = B; tC = C

  // Notes on the sheet:
  //   PROBLEM 3: SERIES-PARALLEL CIRCUITS OF TRANSISTORS
  //   RESERVED SECTION: Do not change anything here!
  //   You may only change the values of the inputs for testing using the hand tool.
  //   Do not introduce any other input or output pins.
  //   From your pull-down circuit
endmodule

module P4_Main (
  input  A4,
  input  A3,
  input  A2,
  input  A1,
  input  A0,
  output X4,
  output X3,
  output X2,
  output X1,
  output X0
);

  wire p4_incrbit0_1_cout, p4_incronebit_1_cout, p4_incronebit_2_cout, p4_incronebit_3_cout;

  P4_IncrBit0 p4_incrbit0_1 (.A(A0), .S(X0), .Cout(p4_incrbit0_1_cout));
  P4_IncrOneBit p4_incronebit_1 (.Cin(p4_incrbit0_1_cout), .A(A1), .S(X1), .Cout(p4_incronebit_1_cout));
  P4_IncrOneBit p4_incronebit_2 (.Cin(p4_incronebit_1_cout), .A(A2), .S(X2), .Cout(p4_incronebit_2_cout));
  P4_IncrOneBit p4_incronebit_3 (.Cin(p4_incronebit_2_cout), .A(A3), .S(X3), .Cout(p4_incronebit_3_cout));
  P4_IncrOneBit p4_incronebit_4 (.Cin(p4_incronebit_3_cout), .A(A4), .S(X4));  // open: Cout

  // Notes on the sheet:
  //   PROBLEM 4: 5-BIT INCREMENTER (Main)
  //   INPUT SECTION: Do not change anything here!
  //   You may only change the values of the inputs for testing using the hand tool.
  //   Do not introduce any other input or output pins.
  //   To your logic
  //   OUTPUT SECTION: Do not change anything here!
  //   Do not introduce any other input or output pins.
  //   From your logic
endmodule

module P4_IncrOneBit (
  input  Cin,
  input  A,
  output S,
  output Cout
);

  xor xor_1 (S, Cin, A);
  and and_1 (Cout, Cin, A);

  // Notes on the sheet:
  //   PROBLEM 4: 12-BIT INCREMENTER (IncrOneBit)
  //   INPUT SECTION: Do not change anything here!
  //   You may only change the values of the inputs for testing using the hand tool.
  //   Do not introduce any other input or output pins.
  //   To your logic
  //   OUTPUT SECTION: Do not change anything here!
  //   Do not introduce any other input or output pins.
  //   From your logic
endmodule

module P4_IncrBit0 (
  input  A,
  output S,
  output Cout
);

  and and_1 (Cout, A, 1'b1);
  not not_1 (S, Cout);

  // Notes on the sheet:
  //   PROBLEM 4: 12-BIT INCREMENTER (IncrBit0)
  //   INPUT SECTION: Do not change anything here!
  //   You may only change the values of the inputs for testing using the hand tool.
  //   Do not introduce any other input or output pins.
  //   To your logic
  //   OUTPUT SECTION: Do not change anything here!
  //   Do not introduce any other input or output pins.
  //   From your logic
endmodule

module P5_Main (
  input  A9,
  input  A8,
  input  A7,
  input  A6,
  input  A5,
  input  A4,
  input  A3,
  input  A2,
  input  A1,
  input  A0,
  output X9,
  output X8,
  output X7,
  output X6,
  output X5,
  output X4,
  output X3,
  output X2,
  output X1,
  output X0
);

  wire [9:0] p5_clsh1_1_y, p5_clsh1_2_y, p5_clsh1_3_y, p5_clsh1_4_y, p5_clsh1_5_y, p5_clsh1_6_y,
       p5_clsh1_7_y, p5_clsh1_8_y;

  P5_CLSH1 p5_clsh1_1 (.X({A9, A8, A7, A6, A5, A4, A3, A2, A1, A0}), .Y(p5_clsh1_1_y));
  P5_CLSH1 p5_clsh1_2 (.X(p5_clsh1_1_y), .Y(p5_clsh1_2_y));
  P5_CLSH1 p5_clsh1_3 (.X(p5_clsh1_2_y), .Y(p5_clsh1_3_y));
  P5_CLSH1 p5_clsh1_4 (.X(p5_clsh1_3_y), .Y(p5_clsh1_4_y));
  P5_CLSH1 p5_clsh1_5 (.X(p5_clsh1_4_y), .Y(p5_clsh1_5_y));
  P5_CLSH1 p5_clsh1_6 (.X(p5_clsh1_5_y), .Y(p5_clsh1_6_y));
  P5_CLSH1 p5_clsh1_7 (.X(p5_clsh1_6_y), .Y(p5_clsh1_7_y));
  P5_CLSH1 p5_clsh1_8 (.X(p5_clsh1_7_y), .Y(p5_clsh1_8_y));
  P5_CLSH1 p5_clsh1_9 (.X(p5_clsh1_8_y), .Y({X9, X8, X7, X6, X5, X4, X3, X2, X1, X0}));

  // Notes on the sheet:
  //   PROBLEM 5: 10-BIT LEFT NORMALIZER (Main)
  //   INPUT SECTION: Do not change anything here!
  //   You may only change the values of the inputs for testing using the hand tool.
  //   Do not introduce any other input or output pins.
  //   To your logic
  //   OUTPUT SECTION: Do not change anything here!
  //   Do not introduce any other input or output pins.
  //   From your logic
endmodule

module P5_LSH1 (
  input  [9:0] X,
  output [9:0] Y
);

  not not_1 (Y[0], 1'b1);

  assign Y[9:1] = X[8:0];

  // Notes on the sheet:
  //   PROBLEM 5: 10-BIT LEFT NORMALIZER (LSH1)
  //   INPUT SECTION: Do not change anything here!
  //   You may only change the values of the inputs for testing using the hand tool.
  //   Do not introduce any other input or output pins.
  //   To your logic
  //   OUTPUT SECTION: Do not change anything here!
  //   Do not introduce any other input or output pins.
  //   From your logic
endmodule

module P5_Mux11 (
  input  S,
  input  [9:0] A,
  input  [9:0] B,
  output [9:0] X
);

  wire not_1_out;
  wire [9:0] and_5_out, and_15_out;

  not not_1 (not_1_out, S);
  and and_1 (and_15_out[6], A[6], not_1_out);
  and and_2 (and_15_out[7], A[7], not_1_out);
  and and_3 (and_15_out[8], A[8], not_1_out);
  and and_4 (and_15_out[9], A[9], not_1_out);
  and and_5 (and_5_out[0], B[0], S);
  and and_6 (and_5_out[1], B[1], S);
  and and_7 (and_5_out[2], B[2], S);
  and and_8 (and_5_out[3], B[3], S);
  and and_9 (and_5_out[4], B[4], S);
  and and_10 (and_5_out[5], B[5], S);
  and and_11 (and_5_out[6], B[6], S);
  and and_12 (and_5_out[7], B[7], S);
  and and_13 (and_5_out[8], B[8], S);
  and and_14 (and_5_out[9], B[9], S);
  and and_15 (and_15_out[0], A[0], not_1_out);
  and and_16 (and_15_out[1], A[1], not_1_out);
  and and_17 (and_15_out[2], A[2], not_1_out);
  and and_18 (and_15_out[3], A[3], not_1_out);
  and and_19 (and_15_out[4], A[4], not_1_out);
  and and_20 (and_15_out[5], A[5], not_1_out);
  assign X = and_5_out | and_15_out;  // OR_Gate or_1, 10 bits wide

  // Notes on the sheet:
  //   PROBLEM 5: 10-BIT LEFT NORMALIZER
  //   INPUT SECTION: Do not change anything here!
  //   You may only change the values of the inputs for testing using the hand tool.
  //   Do not introduce any other input or output pins.
  //   To your logic
  //   OUTPUT SECTION: Do not change anything here!
  //   Do not introduce any other input or output pins.
  //   From your logic
endmodule

module P5_CLSH1 (
  input  [9:0] X,
  output [9:0] Y
);

  wire [9:0] p5_lsh1_1_y;

  P5_LSH1 p5_lsh1_1 (.X(X), .Y(p5_lsh1_1_y));
  P5_Mux11 p5_mux11_1 (.S(X[9]), .A(p5_lsh1_1_y), .B(X), .X(Y));

  // Notes on the sheet:
  //   PROBLEM 5: 10-BIT LEFT NORMALIZER (CLSH1)
  //   INPUT SECTION: Do not change anything here!
  //   You may only change the values of the inputs for testing using the hand tool.
  //   Do not introduce any other input or output pins.
  //   To your logic
  //   OUTPUT SECTION: Do not change anything here!
  //   Do not introduce any other input or output pins.
  //   From your logic
endmodule
